// Logisim project regfile.circ as structural Verilog: 1 circuit, main circuit regfile
module regfile (
  input  [4:0] ReadIndex1,
  input  [4:0] ReadIndex2,
  input  [4:0] WriteIndex,
  input  [31:0] WriteData,
  input  RegWEn,
  input  clk,
  output [31:0] ra,
  output [31:0] sp,
  output [31:0] t0,
  output [31:0] t1,
  output [31:0] t2,
  output [31:0] s0,
  output [31:0] s1,
  output [31:0] a0,
  output [31:0] ReadData1,
  output [31:0] ReadData2
);

  wire [7:0] x0_q;

  // Demultiplexer demultiplexer_1: pin names not known; wires that end beside it: ReadIndex1, ReadIndex2
  Register x0 (.clk(clk), .Q(x0_q));  // open: D, en, clr
  // also tied to GND on the sheet: {x0_q[0], x0_q[1], x0_q[2], x0_q[3], x0_q[4], x0_q[5], x0_q[6], x0_q[7]}

  // Notes on the sheet:
  //   INPUTS to your circuit
  //   DON'T CHANGE THE LOCATIONS OF THE INPUTS AND OUTPUTS!
  //   These are DEBUG/TEST outputs from your circuit.
  //   OUTPUTS from your circuit
endmodule
